# Fritzing sketch Controller (saved by Fritzing 0.7.5b)
breadboards: 1

parts:
  LCD1 = LCD screen
  U1 = atmega328 [package=dip]
  XTAL1 = Crystal [frequency="16 Mhz" package=THT]
  C1 = Ceramic Capacitor [capacitance=20pF package="100 mil [THT, multilayer]"]
  C2 = Ceramic Capacitor [capacitance=20pF package="100 mil [THT, multilayer]"]
  R1 = Rotary Potentiometer (Small) [maximum_resistance=100kΩ]
  R2 = Resistor [tolerance=±5% resistance=220 package=THT]
  S2 = Pushbutton [package="[THT]"]
  R5 = Resistor [tolerance=±5% resistance=10k package=THT]
  R6 = Resistor [tolerance=±5% resistance=100 package=THT]
  S3 = Pushbutton [package="[THT]"]
  R7 = Resistor [tolerance=±5% resistance=10k package=THT]
  R8 = Resistor [tolerance=±5% resistance=100 package=THT]
  S5 = Pushbutton [package="[THT]"]
  R11 = Resistor [tolerance=±5% resistance=10k package=THT]
  R12 = Resistor [tolerance=±5% resistance=100 package=THT]
  LED1 = LED - 5mm [color="Red (633nm)" package="5 mm [THT]"]
  S6 = Pushbutton [package="[THT]"]
  R13 = Resistor [tolerance=±5% resistance=10k package=THT]
  R14 = Resistor [tolerance=±5% resistance=100 package=THT]
  S7 = Pushbutton [package="[THT]"]
  R17 = Resistor [tolerance=±5% resistance=10k package=THT]

nets:
  GND: LCD1.VSS, LCD1.R/W, LCD1.LED-, U1.GND, C1.1, C2.1, R1.leg1, S2.Pin_3, S2.Pin_4, S3.Pin_4, S5.Pin_4, LED1.cathode, S6.Pin_3, S6.Pin_4, S7.Pin_3, S7.Pin_4
  5V: LCD1.VDD, U1.VCC, U1.AVCC, U1.AREF, R1.leg2, R2.Pin_1, R5.Pin_0, R7.Pin_0, R11.Pin_0, R13.Pin_0, R17.Pin_0
  N1: LCD1.V0, R1.wiper
  N2: LCD1.RS, U1.D8
  N3: LCD1.E, U1.D6_(PWM)
  N4: LCD1.DB4, U1.A4
  N5: LCD1.DB5, U1.A3
  N6: LCD1.DB6, U1.A2
  N7: LCD1.DB7, U1.A1
  N8: LCD1.LED+, R2.Pin_0
  N9: U1.RESET, S7.Pin_2, R17.Pin_1
  N10: U1.XLAT1, XTAL1.pin_0, C1.0
  N11: U1.XLAT2, XTAL1.pin_1, C2.0
  N12: U1.D9_(PWM), R12.Pin_0
  N13: U1.D10_(PWM), R8.Pin_0
  N14: U1.D11_(PWM), R6.Pin_0
  N15: U1.D12, R14.Pin_0
  N16: U1.D13, LED1.anode
  N17: S2.Pin_1, S2.Pin_2, R5.Pin_1, R6.Pin_1
  N18: S3.Pin_1, S3.Pin_2, R7.Pin_1, R8.Pin_1
  N19: S5.Pin_1, S5.Pin_2, R11.Pin_1, R12.Pin_1
  N20: S6.Pin_1, S6.Pin_2, R13.Pin_1, R14.Pin_1
